// Logisim project Lab1_computadores.circ as structural Verilog: 13 circuits, main circuit main
module main (
  input  [15:0] in_1,
  input  [15:0] in_2,
  input  [2:0] in_3
);

  wire a1_1_a, a1_1_b, a1_1_c, a1_1_d, a1_1_e, a1_1_f, a1_1_g, a1_2_a, a1_2_b, a1_2_c, a1_2_d, a1_2_e,
       a1_2_f, a1_2_g, a1_3_a, a1_3_b, a1_3_c, a1_3_d, a1_3_e, a1_3_f, a1_3_g, a1_4_a, a1_4_b, a1_4_c,
       a1_4_d, a1_4_e, a1_4_f, a1_4_g, a1_5_a, a1_5_b, a1_5_c, a1_5_d, a1_5_e, a1_5_f, a1_5_g,
       alu_bit_16_1_out_6, alu_bit_16_1_zero;
  wire [3:0] undece_1_out_3;
  wire [15:0] alu_bit_16_1_out_4, undece_1_out_2, undece_1_out_4, undece_1_out_5, undece_1_out_6;
  wire [15:4] undece_1_out_3_2;

  a1 a1_1 (
    .in_1(undece_1_out_2[3:0]), .A(a1_1_a), .B(a1_1_b), .C(a1_1_c), .D(a1_1_d), .E(a1_1_e), .F(a1_1_f),
    .G(a1_1_g));
  LED _15 (.in(alu_bit_16_1_out_4[15]));
  _7_Segment_Display u_7_segment_display_1 (
    .g(a1_1_g), .f(a1_1_f), .a(a1_1_a), .b(a1_1_b), .e(a1_1_e), .d(a1_1_d), .c(a1_1_c));  // open: dp
  LED led_1 ();  // open: in
  LED _14 (.in(alu_bit_16_1_out_4[14]));
  LED _12 (.in(alu_bit_16_1_out_4[12]));
  LED _13 (.in(alu_bit_16_1_out_4[13]));
  LED overFlow (.in(alu_bit_16_1_out_6));
  ALU_bit_16 alu_bit_16_1 (
    .in_1(in_1), .in_2(in_3), .in_3(in_2), .out_4(alu_bit_16_1_out_4), .out_6(alu_bit_16_1_out_6),
    .zero(alu_bit_16_1_zero));  // open: out_7, out_5
  a1 a1_2 (.in_1(undece_1_out_3), .A(a1_2_a), .B(a1_2_b), .C(a1_2_c), .D(a1_2_d), .E(a1_2_e), .F(a1_2_f), .G(a1_2_g));
  LED led_2 ();  // open: in
  LED led_3 ();  // open: in
  LED _10 (.in(alu_bit_16_1_out_4[10]));
  LED _9 (.in(alu_bit_16_1_out_4[9]));
  LED _11 (.in(alu_bit_16_1_out_4[11]));
  LED zero (.in(alu_bit_16_1_zero));
  _7_Segment_Display u_7_segment_display_2 (
    .g(a1_2_g), .f(a1_2_f), .a(a1_2_a), .b(a1_2_b), .e(a1_2_e), .d(a1_2_d), .c(a1_2_c));  // open: dp
  LED _7 (.in(alu_bit_16_1_out_4[7]));
  LED _8 (.in(alu_bit_16_1_out_4[8]));
  a1 a1_3 (
    .in_1(undece_1_out_4[3:0]), .A(a1_3_a), .B(a1_3_b), .C(a1_3_c), .D(a1_3_d), .E(a1_3_e), .F(a1_3_f),
    .G(a1_3_g));
  LED _6 (.in(alu_bit_16_1_out_4[6]));
  LED _5 (.in(alu_bit_16_1_out_4[5]));
  LED _4 (.in(alu_bit_16_1_out_4[4]));
  _7_Segment_Display u_7_segment_display_3 (
    .g(a1_3_g), .f(a1_3_f), .a(a1_3_a), .b(a1_3_b), .e(a1_3_e), .d(a1_3_d), .c(a1_3_c));  // open: dp
  LED _2 (.in(alu_bit_16_1_out_4[2]));
  LED _3 (.in(alu_bit_16_1_out_4[3]));
  LED _1 (.in(alu_bit_16_1_out_4[1]));
  UnDeCe undece_1 (
    .out_4(undece_1_out_4), .out_5(undece_1_out_5), .out_6(undece_1_out_6), .in_1(alu_bit_16_1_out_4),
    .out_3({undece_1_out_3_2, undece_1_out_3}), .out_2(undece_1_out_2));
  a1 a1_4 (
    .in_1(undece_1_out_5[3:0]), .A(a1_4_a), .B(a1_4_b), .C(a1_4_c), .D(a1_4_d), .E(a1_4_e), .F(a1_4_f),
    .G(a1_4_g));
  LED _0 (.in(alu_bit_16_1_out_4[0]));
  _7_Segment_Display u_7_segment_display_4 (
    .g(a1_4_g), .f(a1_4_f), .a(a1_4_a), .b(a1_4_b), .e(a1_4_e), .d(a1_4_d), .c(a1_4_c));  // open: dp
  a1 a1_5 (
    .in_1(undece_1_out_6[3:0]), .A(a1_5_a), .B(a1_5_b), .C(a1_5_c), .D(a1_5_d), .E(a1_5_e), .F(a1_5_f),
    .G(a1_5_g));
  _7_Segment_Display u_7_segment_display_5 (
    .g(a1_5_g), .f(a1_5_f), .a(a1_5_a), .b(a1_5_b), .e(a1_5_e), .d(a1_5_d), .c(a1_5_c));  // open: dp
endmodule

module Sumador (
  input  A,
  input  B,
  input  Cin,
  output S,
  output Cout
);

  wire and_1_out, and_2_out, and_3_out, and_4_out, and_5_out, and_6_out, and_7_out, not_1_out, not_2_out,
       not_3_out, not_4_out, not_5_out, not_6_out;

  not not_1 (not_1_out, A);
  not not_2 (not_2_out, B);
  not not_3 (not_3_out, A);
  not not_4 (not_4_out, Cin);
  not not_5 (not_5_out, B);
  not not_6 (not_6_out, Cin);
  and and_1 (and_1_out, B, Cin);
  and and_2 (and_2_out, A, Cin);
  and and_3 (and_3_out, A, B);
  and and_4 (and_4_out, not_1_out, not_2_out, Cin);
  and and_5 (and_5_out, not_3_out, B, not_4_out);
  and and_6 (and_6_out, A, not_5_out, not_6_out);
  and and_7 (and_7_out, A, B, Cin);
  or or_1 (Cout, and_1_out, and_2_out, and_3_out);
  or or_2 (S, and_4_out, and_5_out, and_6_out, and_7_out);
endmodule

module Sumador_overflow (
  input  A,
  input  B,
  input  Cin,
  output S,
  output Cout,
  output Overflow
);

  wire and_1_out, and_2_out, and_3_out, and_4_out, and_5_out, and_6_out, and_7_out, and_8_out, and_9_out,
       not_1_out, not_2_out, not_3_out, not_4_out, not_5_out, not_6_out, not_7_out;

  not not_1 (not_1_out, A);
  not not_2 (not_2_out, B);
  not not_3 (not_3_out, A);
  not not_4 (not_4_out, Cin);
  not not_5 (not_5_out, B);
  not not_6 (not_6_out, Cin);
  and and_1 (and_1_out, B, Cin);
  and and_2 (and_2_out, A, Cin);
  and and_3 (and_3_out, A, B);
  and and_4 (and_4_out, not_1_out, not_2_out, Cin);
  and and_5 (and_5_out, not_3_out, B, not_4_out);
  and and_6 (and_6_out, A, not_5_out, not_6_out);
  and and_7 (and_7_out, A, B, Cin);
  or or_1 (Cout, and_1_out, and_2_out, and_3_out);
  not not_7 (not_7_out, Cout);
  or or_2 (S, and_4_out, and_5_out, and_6_out, and_7_out);
  and and_8 (and_8_out, not_7_out, Cin);
  and and_9 (and_9_out, not_6_out, Cout);
  or or_3 (Overflow, and_8_out, and_9_out);
endmodule

module ALU_bit_1 (
  input  A,
  input  B,
  input  Cint,
  input  SLT,
  input  Binvert,
  input  [2:0] Op,
  output R,
  output Cout
);

  wire and_1_out, multiplexer_1_out, not_1_out, not_2_out, or_1_out, sumador_1_s;

  not not_1 (not_1_out, B);
  Multiplexer multiplexer_1 (.in0(B), .in1(not_1_out), .out(multiplexer_1_out), .sel(Binvert));  // open: en
  and and_1 (and_1_out, B, A);
  or or_1 (or_1_out, B, A);
  not not_2 (not_2_out, or_1_out);
  Sumador sumador_1 (.A(A), .B(multiplexer_1_out), .Cin(Cint), .S(sumador_1_s), .Cout(Cout));
  Multiplexer #(.select(3), .enable("false")) multiplexer_2 (
    .in0(and_1_out), .in1(sumador_1_s), .in3(sumador_1_s), .in4(not_2_out), .in6(or_1_out), .in7(SLT),
    .out(R), .sel(Op));  // open: in2, in5
endmodule

// A12
module ALU_bit_16 (
  input  [15:0] in_1,
  input  [2:0] in_2,
  input  [15:0] in_3,
  output [15:0] out_4,
  output out_5,
  output out_6,
  output out_7,
  output zero
);

  wire alu_bit_1_1_cout, alu_bit_1_2_cout, alu_bit_1_3_cout, alu_bit_1_4_cout, alu_bit_1_5_cout,
       alu_bit_1_6_cout, alu_bit_1_7_cout, alu_bit_1_8_cout, alu_bit_1_9_cout, alu_bit_1_10_cout,
       alu_bit_1_11_cout, alu_bit_1_12_cout, alu_bit_1_13_cout, alu_bit_1_14_cout, alu_bit_1_15_cout,
       and_1_out, and_2_out, and_3_out, and_4_out, or_1_out, or_2_out, or_3_out, R0, R1, R2, R3, R4, R5, R6,
       R7, R8, R9, R10, R11, R12, R13, R14, R15;
  wire [15:0] sll_slr_1_result;

  and and_1 (and_1_out, in_2[2], in_2[1], in_2[0]);
  and and_2 (and_2_out, ~in_2[2], ~in_2[1], in_2[0]);  // AND_Gate
  // Probe on in_1
  or or_1 (or_1_out, and_2_out, and_1_out);
  // Probe on in_3
  ALU_bit_1 alu_bit_1_1 (
    .R(R0), .A(in_1[0]), .B(in_3[0]), .Cint(or_1_out), .Op(in_2), .Cout(alu_bit_1_1_cout),
    .Binvert(or_1_out), .SLT(out_5));
  ALU_bit_1 alu_bit_1_2 (
    .R(R1), .A(in_1[1]), .B(in_3[1]), .Cint(alu_bit_1_1_cout), .Op(in_2), .Cout(alu_bit_1_2_cout),
    .Binvert(or_1_out), .SLT(1'b0));
  ALU_bit_1 alu_bit_1_3 (
    .R(R2), .A(in_1[2]), .B(in_3[2]), .Cint(alu_bit_1_2_cout), .Op(in_2), .Cout(alu_bit_1_3_cout),
    .Binvert(or_1_out), .SLT(1'b0));
  ALU_bit_1 alu_bit_1_4 (
    .R(R3), .A(in_1[3]), .B(in_3[3]), .Cint(alu_bit_1_3_cout), .Op(in_2), .Cout(alu_bit_1_4_cout),
    .Binvert(or_1_out), .SLT(1'b0));
  ALU_bit_1 alu_bit_1_5 (
    .R(R4), .A(in_1[4]), .B(in_3[4]), .Cint(alu_bit_1_4_cout), .Op(in_2), .Cout(alu_bit_1_5_cout),
    .Binvert(or_1_out), .SLT(1'b0));
  ALU_bit_1 alu_bit_1_6 (
    .R(R5), .A(in_1[5]), .B(in_3[5]), .Cint(alu_bit_1_5_cout), .Op(in_2), .Cout(alu_bit_1_6_cout),
    .Binvert(or_1_out), .SLT(1'b0));
  ALU_bit_1 alu_bit_1_7 (
    .R(R6), .A(in_1[6]), .B(in_3[6]), .Cint(alu_bit_1_6_cout), .Op(in_2), .Cout(alu_bit_1_7_cout),
    .Binvert(or_1_out), .SLT(1'b0));
  ALU_bit_1 alu_bit_1_8 (
    .R(R7), .A(in_1[7]), .B(in_3[7]), .Cint(alu_bit_1_7_cout), .Op(in_2), .Cout(alu_bit_1_8_cout),
    .Binvert(or_1_out), .SLT(1'b0));
  ALU_bit_1 alu_bit_1_9 (
    .R(R8), .A(in_1[8]), .B(in_3[8]), .Cint(alu_bit_1_8_cout), .Op(in_2), .Cout(alu_bit_1_9_cout),
    .Binvert(or_1_out), .SLT(1'b0));
  ALU_bit_1 alu_bit_1_10 (
    .R(R9), .A(in_1[9]), .B(in_3[9]), .Cint(alu_bit_1_9_cout), .Op(in_2), .Cout(alu_bit_1_10_cout),
    .Binvert(or_1_out), .SLT(1'b0));
  ALU_bit_1 alu_bit_1_11 (
    .R(R10), .A(in_1[10]), .B(in_3[10]), .Cint(alu_bit_1_10_cout), .Op(in_2), .Cout(alu_bit_1_11_cout),
    .Binvert(or_1_out), .SLT(1'b0));
  ALU_bit_1 alu_bit_1_12 (
    .R(R11), .A(in_1[11]), .B(in_3[11]), .Cint(alu_bit_1_11_cout), .Op(in_2), .Cout(alu_bit_1_12_cout),
    .Binvert(or_1_out), .SLT(1'b0));
  ALU_bit_1 alu_bit_1_13 (
    .R(R12), .A(in_1[12]), .B(in_3[12]), .Cint(alu_bit_1_12_cout), .Op(in_2), .Cout(alu_bit_1_13_cout),
    .Binvert(or_1_out), .SLT(1'b0));
  ALU_bit_1 alu_bit_1_14 (
    .R(R13), .A(in_1[13]), .B(in_3[13]), .Cint(alu_bit_1_13_cout), .Op(in_2), .Cout(alu_bit_1_14_cout),
    .Binvert(or_1_out), .SLT(1'b0));
  ALU_bit_1 alu_bit_1_15 (
    .R(R14), .A(in_1[14]), .B(in_3[14]), .Cint(alu_bit_1_14_cout), .Op(in_2), .Cout(alu_bit_1_15_cout),
    .Binvert(or_1_out), .SLT(1'b0));
  ALU_BIT_1_overflow alu_bit_1_overflow_1 (
    .A(in_1[15]), .B(in_3[15]), .Cint(alu_bit_1_15_cout), .R(R15), .overFlow(out_6), .Cout(out_7), .Op(in_2),
    .Binvert(or_1_out), .SLT(1'b0), .slt_2(out_5));
  // Probe on out_4
  Multiplexer #(.width(16), .enable("false")) multiplexer_1 (
    .in0({R15, R14, R13, R12, R11, R10, R9, R8, R7, R6, R5, R4, R3, R2, R1, R0}), .in1(sll_slr_1_result),
    .out(out_4), .sel(or_2_out));
  or or_2 (or_2_out, and_4_out, and_3_out);
  and and_3 (and_3_out, ~in_2[2], in_2[1], ~in_2[0]);  // AND_Gate
  and and_4 (and_4_out, in_2[2], ~in_2[1], in_2[0]);  // AND_Gate
  sll_slr sll_slr_1 (.A(in_1), .B(in_3), .OP(in_2), .Result(sll_slr_1_result));
  or or_3 (or_3_out, R0, R1, R2, R3, R4, R5, R6, R7, R8, R9, R10, R11, R12, R13, R14, R15);
  not not_1 (zero, or_3_out);

  // Other names for the same wires on the sheet: A[15:0] = in_1; A0 = in_1[0]; A1 = in_1[1]; A2 = in_1[2];
  //   A3 = in_1[3]; A4 = in_1[4]; A5 = in_1[5]; A6 = in_1[6]; A7 = in_1[7]; A8 = in_1[8]; A9 = in_1[9];
  //   A10 = in_1[10]; A11 = in_1[11]; A12 = in_1[12]; A13 = in_1[13]; A14 = in_1[14]; A15 = in_1[15]; B0 = in_3[0];
  //   Dec[15:0] = in_3; B1 = in_3[1]; B2 = in_3[2]; B3 = in_3[3]; B4 = in_3[4]; B5 = in_3[5]; B6 = in_3[6];
  //   B7 = in_3[7]; B8 = in_3[8]; B9 = in_3[9]; B10 = in_3[10]; B11 = in_3[11]; B12 = in_3[12]; B13 = in_3[13];
  //   B14 = in_3[14]; B15 = in_3[15]; OP[2:0] = in_2; slt = out_5
endmodule

module ALU_BIT_1_overflow (
  input  A,
  input  B,
  input  Cint,
  input  SLT,
  input  Binvert,
  input  [2:0] Op,
  output R,
  output slt_2,
  output overFlow,
  output Cout
);

  wire and_1_out, multiplexer_1_out, not_1_out, not_2_out, or_1_out, or_2_out;

  not not_1 (not_1_out, B);
  Multiplexer multiplexer_1 (.in0(B), .in1(not_1_out), .out(multiplexer_1_out), .sel(Binvert));  // open: en
  and and_1 (and_1_out, B, A);
  or or_1 (or_1_out, B, A);
  not not_2 (not_2_out, or_2_out);
  or or_2 (or_2_out, B, A);
  Sumador_overflow sumador_overflow_1 (
    .A(multiplexer_1_out), .B(A), .Cin(Cint), .S(slt_2), .Cout(Cout), .Overflow(overFlow));
  Multiplexer #(.select(3), .enable("false")) multiplexer_2 (
    .in0(and_1_out), .in1(slt_2), .in3(slt_2), .in4(not_2_out), .in6(or_1_out), .in7(SLT), .out(R), .sel(Op));  // open: in2, in5
endmodule

module Decoder (
  input  [15:0] in_1,
  output [15:0] out_2
);

  wire nor_1_out;
  wire [15:0] and_1_out;

  and and_1 (and_1_out[0], ~in_1[0], ~in_1[1], ~in_1[2], ~in_1[3]);  // AND_Gate
  and and_2 (and_1_out[1], in_1[0], ~in_1[1], ~in_1[2], ~in_1[3]);  // AND_Gate
  and and_3 (and_1_out[2], ~in_1[0], in_1[1], ~in_1[2], ~in_1[3]);  // AND_Gate
  and and_4 (and_1_out[3], in_1[0], in_1[1], ~in_1[2], ~in_1[3]);  // AND_Gate
  and and_5 (and_1_out[4], ~in_1[0], ~in_1[1], in_1[2], ~in_1[3]);  // AND_Gate
  and and_6 (and_1_out[5], in_1[0], ~in_1[1], in_1[2], ~in_1[3]);  // AND_Gate
  and and_7 (and_1_out[6], ~in_1[0], in_1[1], in_1[2], ~in_1[3]);  // AND_Gate
  and and_8 (and_1_out[7], in_1[0], in_1[1], in_1[2], ~in_1[3]);  // AND_Gate
  and and_9 (and_1_out[8], ~in_1[0], ~in_1[1], ~in_1[2], in_1[3]);  // AND_Gate
  and and_10 (and_1_out[9], in_1[0], ~in_1[1], ~in_1[2], in_1[3]);  // AND_Gate
  and and_11 (and_1_out[10], ~in_1[0], in_1[1], ~in_1[2], in_1[3]);  // AND_Gate
  and and_12 (and_1_out[11], in_1[0], in_1[1], ~in_1[2], in_1[3]);  // AND_Gate
  and and_13 (and_1_out[12], ~in_1[0], ~in_1[1], in_1[2], in_1[3]);  // AND_Gate
  and and_14 (and_1_out[13], in_1[0], ~in_1[1], in_1[2], in_1[3]);  // AND_Gate
  and and_15 (and_1_out[14], ~in_1[0], in_1[1], in_1[2], in_1[3]);  // AND_Gate
  and and_16 (and_1_out[15], in_1[0], in_1[1], in_1[2], in_1[3]);
  nor nor_1 (nor_1_out, in_1[4], in_1[5], in_1[6], in_1[7], in_1[8], in_1[9], in_1[11], in_1[12], in_1[13], in_1[14], in_1[15], in_1[10]);
  Multiplexer #(.width(16), .enable("false")) multiplexer_1 (
    .in0({16{1'b1}}), .in1(and_1_out), .out(out_2), .sel(nor_1_out));
endmodule

module SLR_SLL (
  input  [2:0] Ope,
  input  [15:0] A,
  input  [15:0] B,
  output [15:0] out_4
);

  wire and_1_out;
  wire [15:0] divider_1_out, multiplier_1_out;

  Multiplier #(.width(16)) multiplier_1 (.a(A), .b(B), .out(multiplier_1_out));  // open: cin, cout
  Divider #(.width(16)) divider_1 (.a(A), .b(B), .out(divider_1_out));  // open: upper, rem
  and and_1 (and_1_out, ~Ope[2], Ope[1], ~Ope[0]);  // AND_Gate
  Multiplexer #(.width(16), .disabled(0), .enable("false")) multiplexer_1 (
    .in0(multiplier_1_out), .in1(divider_1_out), .out(out_4), .sel(and_1_out));
endmodule

module _7_Seg (
  input  [3:0] in_1
);
endmodule

module a1 (
  input  [3:0] in_1,
  output A,
  output B,
  output C,
  output D,
  output E,
  output F,
  output G
);

  wire and_1_out, and_2_out, and_3_out, and_4_out, and_5_out, and_6_out, and_7_out, and_8_out, and_9_out,
       and_10_out, and_11_out, and_12_out, and_13_out, and_14_out, and_15_out, and_16_out, and_17_out,
       and_18_out, and_19_out, and_20_out, and_21_out, and_22_out, and_23_out, and_24_out, and_25_out,
       and_26_out;

  and and_1 (and_1_out, ~in_1[2], ~in_1[1], ~in_1[0]);  // AND_Gate
  and and_2 (and_2_out, in_1[3], ~in_1[2], ~in_1[1]);  // AND_Gate
  and and_3 (and_3_out, ~in_1[3], in_1[2], in_1[0]);  // AND_Gate
  and and_4 (and_4_out, ~in_1[3], in_1[1]);  // AND_Gate
  and and_5 (and_5_out, ~in_1[3], ~in_1[1], ~in_1[0]);  // AND_Gate
  and and_6 (and_6_out, ~in_1[3], in_1[1], in_1[0]);  // AND_Gate
  and and_7 (and_7_out, ~in_1[3], ~in_1[2]);  // AND_Gate
  and and_8 (and_8_out, ~in_1[2], ~in_1[1]);  // AND_Gate
  and and_9 (and_9_out, ~in_1[2], ~in_1[1]);  // AND_Gate
  and and_10 (and_10_out, ~in_1[3], in_1[2]);  // AND_Gate
  and and_11 (and_11_out, ~in_1[3], in_1[0]);  // AND_Gate
  and and_12 (and_12_out, ~in_1[1], ~in_1[2], ~in_1[0]);  // AND_Gate
  and and_13 (and_13_out, ~in_1[3], in_1[2], ~in_1[1], in_1[0]);  // AND_Gate
  and and_14 (and_14_out, ~in_1[3], ~in_1[2], in_1[1]);  // AND_Gate
  and and_15 (and_15_out, ~in_1[3], in_1[1], ~in_1[0]);  // AND_Gate
  and and_16 (and_16_out, in_1[3], ~in_1[2], ~in_1[1]);  // AND_Gate
  and and_17 (and_17_out, ~in_1[2], ~in_1[1], ~in_1[0]);  // AND_Gate
  and and_18 (and_18_out, ~in_1[3], in_1[1], ~in_1[0]);  // AND_Gate
  and and_19 (and_19_out, ~in_1[2], ~in_1[1], ~in_1[0]);  // AND_Gate
  and and_20 (and_20_out, ~in_1[3], in_1[2], ~in_1[1]);  // AND_Gate
  and and_21 (and_21_out, ~in_1[3], in_1[2], ~in_1[0]);  // AND_Gate
  and and_22 (and_22_out, in_1[3], ~in_1[2], ~in_1[1]);  // AND_Gate
  and and_23 (and_23_out, ~in_1[3], ~in_1[2], in_1[1]);  // AND_Gate
  and and_24 (and_24_out, ~in_1[3], in_1[2], ~in_1[1]);  // AND_Gate
  and and_25 (and_25_out, ~in_1[3], in_1[1], ~in_1[0]);  // AND_Gate
  and and_26 (and_26_out, in_1[3], ~in_1[2], ~in_1[1]);  // AND_Gate
  or or_1 (A, and_1_out, and_2_out, and_3_out, and_4_out);
  or or_2 (B, and_5_out, and_6_out, and_7_out, and_8_out);
  or or_3 (C, and_9_out, and_10_out, and_11_out);
  or or_4 (E, and_17_out, and_18_out);
  or or_5 (D, and_12_out, and_13_out, and_14_out, and_15_out, and_16_out);
  or or_6 (F, and_19_out, and_20_out, and_21_out, and_22_out);
  or or_7 (G, and_23_out, and_24_out, and_25_out, and_26_out);
endmodule

module UnDeCe (
  input  [15:0] in_1,
  output [15:0] out_2,
  output [15:0] out_3,
  output [15:0] out_4,
  output [15:0] out_5,
  output [15:0] out_6
);

  wire [15:0] complementoa2_1_out_2, divider_1_rem, divider_2_rem, divider_3_rem;

  ComplementoA2 complementoa2_1 (.Entrada_A2(in_1), .out_2(complementoa2_1_out_2));
  Divider #(.width(16)) divider_1 (
    .a(complementoa2_1_out_2), .b(16'h2710), .out(out_2), .rem(divider_1_rem));  // open: upper
  Divider #(.width(16)) divider_2 (.a(divider_1_rem), .b(16'h3e8), .out(out_3), .rem(divider_2_rem));  // open: upper
  Divider #(.width(16)) divider_3 (.a(divider_2_rem), .b(16'h64), .out(out_4), .rem(divider_3_rem));  // open: upper
  Divider #(.width(16)) divider_4 (.a(divider_3_rem), .b(16'ha), .out(out_5), .rem(out_6));  // open: upper
endmodule

module ComplementoA2 (
  input  [15:0] Entrada_A2,
  output [15:0] out_2
);

  wire [15:0] alu_bit_16_1_out_4, not_1_out;

  // Probe on Entrada_A2
  assign not_1_out = ~Entrada_A2;  // NOT_Gate not_1, 16 bits wide
  ALU_bit_16 alu_bit_16_1 (
    .in_1(not_1_out), .in_2(3'b011), .in_3(16'h1), .out_4(alu_bit_16_1_out_4));  // open: out_7, out_5, out_6, zero
  // Probe on alu_bit_16_1_out_4
  // Probe on out_2
  Multiplexer #(.width(16)) multiplexer_1 (
    .in0(Entrada_A2), .in1(alu_bit_16_1_out_4), .out(out_2), .sel(Entrada_A2[15]));  // open: en
  // Probe on alu_bit_16_1_out_4

  // Other names for the same wires on the sheet: Signo = Entrada_A2[15]
endmodule

module sll_slr (
  input  [15:0] A,
  input  [2:0] OP,
  input  [15:0] B,
  output [15:0] Result
);

  wire OP_t, or_1_out;
  wire [15:0] multiplexer_1_out, multiplexer_2_out, multiplexer_3_out, multiplexer_4_out, multiplexer_6_out,
       multiplexer_7_out, multiplexer_8_out, multiplexer_9_out;

  and and_1 (OP_t, ~OP[2], OP[1], ~OP[0]);  // AND_Gate
  Multiplexer #(.width(16)) multiplexer_1 (
    .in0(A), .in1(multiplexer_2_out), .out(multiplexer_1_out), .sel(B[0]));  // open: en
  Multiplexer #(.width(16)) multiplexer_2 (
    .in0({A[14:0], 1'b0}), .in1({1'b0, A[15:1]}), .out(multiplexer_2_out), .sel(OP_t));  // open: en
  or or_1 (or_1_out, B[4], B[5], B[6], B[7], B[8], B[9], B[10], B[11], B[12], B[13], B[14], B[15]);
  Multiplexer #(.width(16)) multiplexer_3 (
    .in0({multiplexer_1_out[13:0], 2'b00}), .in1({2'b00, multiplexer_1_out[15:2]}), .out(multiplexer_3_out),
    .sel(OP_t));  // open: en
  Multiplexer #(.width(16)) multiplexer_4 (
    .in0(multiplexer_1_out), .in1(multiplexer_3_out), .out(multiplexer_4_out), .sel(B[1]));  // open: en
  Multiplexer #(.width(16)) multiplexer_5 (
    .in0(multiplexer_8_out), .in1({16{1'b0}}), .out(Result), .sel(or_1_out));  // open: en
  Multiplexer #(.width(16)) multiplexer_6 (
    .in0({multiplexer_4_out[11:0], 4'b0000}), .in1({4'b0000, multiplexer_4_out[15:4]}),
    .out(multiplexer_6_out), .sel(OP_t));  // open: en
  Multiplexer #(.width(16)) multiplexer_7 (
    .in0(multiplexer_4_out), .in1(multiplexer_6_out), .out(multiplexer_7_out), .sel(B[2]));  // open: en
  Multiplexer #(.width(16)) multiplexer_8 (
    .in0(multiplexer_7_out), .in1(multiplexer_9_out), .out(multiplexer_8_out), .sel(B[3]));  // open: en
  Multiplexer #(.width(16)) multiplexer_9 (
    .in0({multiplexer_7_out[7:0], {8{1'b0}}}), .in1({{8{1'b0}}, multiplexer_7_out[15:8]}),
    .out(multiplexer_9_out), .sel(OP_t));  // open: en
endmodule
