// Logisim project Lab2_computadores.circ as structural Verilog: 9 circuits, main circuit main
module main (
  input  in_1,
  input  in_2,
  input  in_3
);

  wire n7segmentos_1_a, n7segmentos_1_b, n7segmentos_1_c, n7segmentos_1_d, n7segmentos_1_e, n7segmentos_1_f,
       n7segmentos_1_g, n7segmentos_2_a, n7segmentos_2_b, n7segmentos_2_c, n7segmentos_2_d, n7segmentos_2_e,
       n7segmentos_2_f, n7segmentos_2_g, reconocedor_sec_1_s1, reconocedor_sec_1_s2, reconocedor_sec_1_s3,
       reconocedor_sec_1_s4;
  wire [3:0] reconocedor_sec_1_out_6, uni_dec_1_out_2, uni_dec_1_out_3;

  Reconocedor_sec reconocedor_sec_1 (
    .in_1(in_1), .Reset(in_3), .out_6(reconocedor_sec_1_out_6), .S1(reconocedor_sec_1_s1),
    .S2(reconocedor_sec_1_s2), .S3(reconocedor_sec_1_s3), .S4(reconocedor_sec_1_s4), .Clk(in_2));
  LED S2 (.in(reconocedor_sec_1_s2));
  LED S3 (.in(reconocedor_sec_1_s3));
  LED S4 (.in(reconocedor_sec_1_s4));
  LED S1 (.in(reconocedor_sec_1_s1));
  Uni_Dec uni_dec_1 (.in_1(reconocedor_sec_1_out_6), .out_2(uni_dec_1_out_2), .out_3(uni_dec_1_out_3));
  _7segmentos u_7segmentos_1 (
    .in_1(uni_dec_1_out_2), .A(n7segmentos_1_a), .B(n7segmentos_1_b), .C(n7segmentos_1_c),
    .D(n7segmentos_1_d), .E(n7segmentos_1_e), .F(n7segmentos_1_f), .G(n7segmentos_1_g));
  _7_Segment_Display u_7_segment_display_1 (
    .g(n7segmentos_1_g), .f(n7segmentos_1_f), .a(n7segmentos_1_a), .b(n7segmentos_1_b), .e(n7segmentos_1_e),
    .d(n7segmentos_1_d), .c(n7segmentos_1_c));  // open: dp
  _7segmentos u_7segmentos_2 (
    .in_1(uni_dec_1_out_3), .A(n7segmentos_2_a), .B(n7segmentos_2_b), .C(n7segmentos_2_c),
    .D(n7segmentos_2_d), .E(n7segmentos_2_e), .F(n7segmentos_2_f), .G(n7segmentos_2_g));
  _7_Segment_Display u_7_segment_display_2 (
    .g(n7segmentos_2_g), .f(n7segmentos_2_f), .a(n7segmentos_2_a), .b(n7segmentos_2_b), .e(n7segmentos_2_e),
    .d(n7segmentos_2_d), .c(n7segmentos_2_c));  // open: dp
endmodule

module Reconocedor_sec (
  input  in_1,
  input  Reset,
  input  Clk,
  output S1,
  output S2,
  output [3:0] out_6,
  output S3,
  output S4
);

  wire J1, J2, J3, J4, K1, K2, K3, K4;

  J4K4 j4k4_1 (.A(out_6[3]), .B(out_6[2]), .C(out_6[1]), .E(in_1), .J4(J4), .K4(K4));
  J1K1 j1k1_1 (.B(out_6[2]), .C(out_6[1]), .E(in_1), .D(out_6[0]), .J1(J1), .K1(K1));
  J2K2 j2k2_1 (.A(out_6[3]), .C(out_6[1]), .D(out_6[0]), .E(in_1), .J2(J2), .K2(K2));
  J3K3 j3k3_1 (.A(out_6[3]), .B(out_6[2]), .D(out_6[0]), .E(in_1), .J3(J3), .K3(K3));
  Y1Y2Y3Y4 y1y2y3y4_1 (.A(out_6[3]), .B(out_6[2]), .C(out_6[1]), .D(out_6[0]), .Y1(S1), .Y2(S2), .Y3(S3), .Y4(S4));
  J_K_Flip_Flop j_k_ff_1 (.J(J4), .clk(Clk), .K(K4), .Q(out_6[0]), .reset(Reset));  // open: Qn, preset, en
  J_K_Flip_Flop j_k_ff_2 (.J(J3), .clk(Clk), .K(K3), .Q(out_6[1]), .reset(Reset));  // open: Qn, preset, en
  J_K_Flip_Flop j_k_ff_3 (.J(J2), .clk(Clk), .K(K2), .Q(out_6[2]), .reset(Reset));  // open: Qn, preset, en
  J_K_Flip_Flop j_k_ff_4 (.J(J1), .clk(Clk), .K(K1), .Q(out_6[3]), .reset(Reset));  // open: Qn, preset, en

  // Other names for the same wires on the sheet: Q4 = out_6[0]; Q3 = out_6[1]; Q2 = out_6[2]; Q1 = out_6[3]; X = in_1;
  //   Y1 = S1; Y2 = S2; Y3 = S3; Y4 = S4
endmodule

module J2K2 (
  input  A,
  input  C,
  input  D,
  input  E,
  output J2,
  output K2
);

  wire and_1_out, and_2_out, and_3_out, and_4_out, and_5_out, and_6_out, and_7_out;

  and and_1 (and_1_out, ~A, C);  // AND_Gate
  and and_2 (and_2_out, A, E);
  and and_3 (and_3_out, A, ~C, D);  // AND_Gate
  and and_4 (and_4_out, ~D, ~E);  // AND_Gate
  and and_5 (and_5_out, C, E);
  and and_6 (and_6_out, ~A, ~C, ~E);  // AND_Gate
  and and_7 (and_7_out, A, D, E);
  or or_1 (J2, and_1_out, and_2_out, and_3_out);
  or or_2 (K2, and_4_out, and_5_out, and_6_out, and_7_out);
endmodule

module J3K3 (
  input  A,
  input  B,
  input  D,
  input  E,
  output J3,
  output K3
);

  wire and_1_out, and_2_out, and_3_out, and_4_out, and_5_out;

  and and_1 (and_1_out, ~B, E);  // AND_Gate
  and and_2 (and_2_out, ~A, ~B, E);  // AND_Gate
  and and_3 (and_3_out, ~A, ~D, E);  // AND_Gate
  and and_4 (and_4_out, A, ~B, ~D);  // AND_Gate
  and and_5 (and_5_out, A, D, ~E);  // AND_Gate
  or or_1 (J3, and_2_out, and_3_out, and_4_out, and_5_out);
  or or_2 (K3, ~D, A, and_1_out);  // OR_Gate
endmodule

module J4K4 (
  input  A,
  input  B,
  input  C,
  input  E,
  output J4,
  output K4
);

  wire and_1_out, and_2_out, and_3_out, and_4_out, and_5_out, and_6_out, and_7_out, and_8_out, and_9_out;

  and and_1 (and_1_out, C, E);
  and and_2 (and_2_out, ~A, B);  // AND_Gate
  and and_3 (and_3_out, B, C);
  and and_4 (and_4_out, A, E);
  and and_5 (and_5_out, ~B, ~C, ~E);  // AND_Gate
  or or_1 (J4, and_1_out, and_2_out, and_3_out, and_4_out, and_5_out);
  and and_6 (and_6_out, B, ~E);  // AND_Gate
  and and_7 (and_7_out, B, C);
  and and_8 (and_8_out, ~A, C, ~E);  // AND_Gate
  and and_9 (and_9_out, A, ~B, ~C);  // AND_Gate
  or or_2 (K4, and_6_out, and_7_out, and_8_out, and_9_out);
endmodule

module Y1Y2Y3Y4 (
  input  A,
  input  B,
  input  C,
  input  D,
  output Y1,
  output Y2,
  output Y3,
  output Y4
);

  wire and_2_out, and_3_out;

  and and_1 (Y1, A, ~B, ~C, ~D);  // AND_Gate
  and and_2 (and_2_out, A, ~B, C, ~D);  // AND_Gate
  and and_3 (and_3_out, A, B, ~C, ~D);  // AND_Gate
  and and_4 (Y3, A, B, ~C, ~D);  // AND_Gate
  and and_5 (Y4, A, B, C, ~D);  // AND_Gate
  or or_1 (Y2, and_2_out, and_3_out);
endmodule

module J1K1 (
  input  B,
  input  C,
  input  E,
  input  D,
  output J1,
  output K1
);

  wire and_1_out, and_2_out, and_3_out, and_4_out, and_5_out, and_6_out;

  and and_1 (and_1_out, B, C, E);
  and and_2 (and_2_out, B, ~C, D, ~E);  // AND_Gate
  and and_3 (and_3_out, ~B, ~D, E);  // AND_Gate
  and and_4 (and_4_out, ~B, D, ~E);  // AND_Gate
  and and_5 (and_5_out, B, ~C, E);  // AND_Gate
  and and_6 (and_6_out, B, C, ~E);  // AND_Gate
  or or_1 (J1, and_1_out, and_2_out);
  or or_2 (K1, and_3_out, and_4_out, and_5_out, and_6_out);
endmodule

module _7segmentos (
  input  [3:0] in_1,
  output A,
  output B,
  output C,
  output D,
  output E,
  output F,
  output G
);

  wire and_1_out, and_2_out, and_3_out, and_4_out, and_5_out, and_6_out, and_7_out, and_8_out, and_9_out,
       and_10_out, and_11_out, and_12_out, and_13_out, and_14_out, and_15_out, and_16_out, and_17_out,
       and_18_out, and_19_out, and_20_out, and_21_out, and_22_out, and_23_out, and_24_out, and_25_out,
       and_26_out;

  and and_1 (and_1_out, ~in_1[2], ~in_1[1], ~in_1[0]);  // AND_Gate
  and and_2 (and_2_out, in_1[3], ~in_1[2], ~in_1[1]);  // AND_Gate
  and and_3 (and_3_out, ~in_1[3], in_1[2], in_1[0]);  // AND_Gate
  and and_4 (and_4_out, ~in_1[3], in_1[1]);  // AND_Gate
  and and_5 (and_5_out, ~in_1[3], ~in_1[1], ~in_1[0]);  // AND_Gate
  and and_6 (and_6_out, ~in_1[3], in_1[1], in_1[0]);  // AND_Gate
  and and_7 (and_7_out, ~in_1[3], ~in_1[2]);  // AND_Gate
  and and_8 (and_8_out, ~in_1[2], ~in_1[1]);  // AND_Gate
  and and_9 (and_9_out, ~in_1[2], ~in_1[1]);  // AND_Gate
  and and_10 (and_10_out, ~in_1[3], in_1[2]);  // AND_Gate
  and and_11 (and_11_out, ~in_1[3], in_1[0]);  // AND_Gate
  and and_12 (and_12_out, ~in_1[1], ~in_1[2], ~in_1[0]);  // AND_Gate
  and and_13 (and_13_out, ~in_1[3], in_1[2], ~in_1[1], in_1[0]);  // AND_Gate
  and and_14 (and_14_out, ~in_1[3], ~in_1[2], in_1[1]);  // AND_Gate
  and and_15 (and_15_out, ~in_1[3], in_1[1], ~in_1[0]);  // AND_Gate
  and and_16 (and_16_out, in_1[3], ~in_1[2], ~in_1[1]);  // AND_Gate
  and and_17 (and_17_out, ~in_1[2], ~in_1[1], ~in_1[0]);  // AND_Gate
  and and_18 (and_18_out, ~in_1[3], in_1[1], ~in_1[0]);  // AND_Gate
  and and_19 (and_19_out, ~in_1[2], ~in_1[1], ~in_1[0]);  // AND_Gate
  and and_20 (and_20_out, ~in_1[3], in_1[2], ~in_1[1]);  // AND_Gate
  and and_21 (and_21_out, ~in_1[3], in_1[2], ~in_1[0]);  // AND_Gate
  and and_22 (and_22_out, in_1[3], ~in_1[2], ~in_1[1]);  // AND_Gate
  and and_23 (and_23_out, ~in_1[3], ~in_1[2], in_1[1]);  // AND_Gate
  and and_24 (and_24_out, ~in_1[3], in_1[2], ~in_1[1]);  // AND_Gate
  and and_25 (and_25_out, ~in_1[3], in_1[1], ~in_1[0]);  // AND_Gate
  and and_26 (and_26_out, in_1[3], ~in_1[2], ~in_1[1]);  // AND_Gate
  or or_1 (A, and_1_out, and_2_out, and_3_out, and_4_out);
  or or_2 (B, and_5_out, and_6_out, and_7_out, and_8_out);
  or or_3 (C, and_9_out, and_10_out, and_11_out);
  or or_4 (E, and_17_out, and_18_out);
  or or_5 (D, and_12_out, and_13_out, and_14_out, and_15_out, and_16_out);
  or or_6 (F, and_19_out, and_20_out, and_21_out, and_22_out);
  or or_7 (G, and_23_out, and_24_out, and_25_out, and_26_out);
endmodule

module Uni_Dec (
  input  [3:0] in_1,
  output [3:0] out_2,
  output [3:0] out_3
);

  Divider #(.width(4)) divider_1 (.a(in_1), .b(4'b1010), .out(out_2), .rem(out_3));  // open: upper
endmodule
