// Logisim project Lab4 sin componentes.circ as structural Verilog: 6 circuits, main circuit main
module main (
  input  Clear,
  input  [2:0] in_2
);

  wire alu_bit_16_1_zero, ALUSrc, and_1_out, B, Branch, button_1_out, button_2_out, Clock, J, Jump, MemRead,
       MemtoReg, MemWrite, RegDst, RegWrite, SLL_SLR;
  wire [1:0] ALUOp, ALUop_t;
  wire [3:0] multiplexer_1_out, OP;
  wire [15:0] adder_1_out, adder_2_out, alu_bit_16_1_result, bit_extender_1_out, bit_extender_2_out,
       multiplexer_2_out, multiplexer_3_out, multiplexer_4_out, multiplexer_5_out, multiplexer_6_out, PC,
       ram_1_data, Registers_dataread1, Registers_dataread2;
  wire [19:0] rom_1_data;

  Register #(.width(16)) register_1 (.D(multiplexer_5_out), .Q(PC), .clk(Clock), .clr(button_1_out));  // open: en
  Button button_1 (.out(button_1_out));
  Clock clock_1 (.out(Clock));
  shift shift_1 (.in_1(OP), .out_2(SLL_SLR));
  Adder #(.width(16)) adder_1 (.a(16'h1), .b(PC), .out(adder_1_out));  // open: cin, cout
  unitControl unitcontrol_1 (
    .in_1(OP), .RegDst(RegDst), .ALUSrc(ALUSrc), .MemtoReg(MemtoReg), .RegWrite(RegWrite), .MemRead(MemRead),
    .MenWrite(MemWrite), .Branch(B), .ALUOp(ALUop_t), .Jump(J));
  ROM #(.addrWidth(16), .dataWidth(24)) rom_1 (.addr(PC), .data({OP, rom_1_data}));  // open: sel
  // Control Control: pin names not known; wires that end beside it: OP, RegDst, ALUSrc, MemtoReg, RegWrite, MemRead, MemWrite, Branch, ALUOp[1], ALUOp[0], Jump
  Multiplexer #(.width(4)) multiplexer_1 (
    .in0(rom_1_data[15:12]), .in1(rom_1_data[11:8]), .out(multiplexer_1_out), .sel(RegDst));  // open: en
  assign bit_extender_1_out = {{4{1'b0}}, {rom_1_data[3:0], rom_1_data[7:4], rom_1_data[11:8]}};  // Bit_Extender bit_extender_1
  ALU_CONTROL alu_control_1 (.in_1(rom_1_data[3:0]), .in_2(ALUop_t));  // open: out_3
  Registers Registers (
    .DataWrite(multiplexer_6_out), .Clock(Clock), .RegWrite(RegWrite), .WriteRegister(multiplexer_1_out),
    .DataRead1(Registers_dataread1), .ReadRegister1(rom_1_data[19:16]), .DataRead2(Registers_dataread2),
    .ReadRegister2(rom_1_data[15:12]), .Reset(Clear));
  Adder #(.width(16)) adder_2 (.a(adder_1_out), .b(bit_extender_1_out), .out(adder_2_out));  // open: cin, cout
  Multiplexer #(.width(16)) multiplexer_2 (
    .in0(Registers_dataread2), .in1(bit_extender_1_out), .out(multiplexer_2_out), .sel(ALUSrc));  // open: en
  assign bit_extender_2_out = {{12{1'b0}}, rom_1_data[7:4]};  // Bit_Extender bit_extender_2
  Multiplexer #(.width(16)) multiplexer_3 (
    .in0(multiplexer_2_out), .in1(bit_extender_2_out), .out(multiplexer_3_out), .sel(SLL_SLR));  // open: en
  ALU_bit_16 alu_bit_16_1 (
    .A(Registers_dataread1), .in_2(in_2), .B(multiplexer_3_out), .Result(alu_bit_16_1_result),
    .zero(alu_bit_16_1_zero));  // open: out_5
  and and_1 (and_1_out, B, alu_bit_16_1_zero);
  Multiplexer #(.width(16)) multiplexer_4 (
    .in0(adder_1_out), .in1(adder_2_out), .out(multiplexer_4_out), .sel(and_1_out));  // open: en
  Multiplexer #(.width(16)) multiplexer_5 (
    .in0(multiplexer_4_out), .in1(rom_1_data[15:0]), .out(multiplexer_5_out), .sel(J));  // open: en
  RAM #(.addrWidth(16), .dataWidth(16), .bus("separate")) ram_1 (
    .addr(alu_bit_16_1_result), .din(Registers_dataread2), .data(ram_1_data), .str(MemWrite), .sel(Clock),
    .ld(MemRead), .clr(button_2_out));  // open: clk
  Button button_2 (.out(button_2_out));
  Multiplexer #(.width(16)) multiplexer_6 (
    .in0(alu_bit_16_1_result), .in1(ram_1_data), .out(multiplexer_6_out), .sel(MemtoReg));  // open: en

  // Other names for the same wires on the sheet: ALUOperation[2:0] = in_2

  // Notes on the sheet:
  //   contents of rom_1 (hex, n*v repeats v):
  //   303 a403 127000
endmodule

module Registers (
  input  [15:0] DataWrite,
  input  Clock,
  input  [3:0] ReadRegister1,
  input  RegWrite,
  input  [3:0] WriteRegister,
  input  [3:0] ReadRegister2,
  input  Reset,
  output [15:0] DataRead1,
  output [15:0] DataRead2
);

  wire decoder_1_out1, decoder_1_out2, decoder_1_out3, decoder_1_out4, decoder_1_out5, decoder_1_out6,
       decoder_1_out7, decoder_1_out8, decoder_1_out9, decoder_1_out10, decoder_1_out11, decoder_1_out12,
       decoder_1_out13, decoder_1_out14, decoder_1_out15;
  wire [15:0] register_1_q, register_2_q, register_3_q, register_4_q, register_5_q, register_6_q,
       register_7_q, register_8_q, register_9_q, register_10_q, register_11_q, register_12_q, register_13_q,
       register_14_q, register_15_q, register_16_q;

  Decoder #(.select(4), .disabled(0)) decoder_1 (
    .out1(decoder_1_out1), .out2(decoder_1_out2), .out3(decoder_1_out3), .out4(decoder_1_out4),
    .out5(decoder_1_out5), .out6(decoder_1_out6), .out7(decoder_1_out7), .out8(decoder_1_out8),
    .out9(decoder_1_out9), .out10(decoder_1_out10), .out11(decoder_1_out11), .out12(decoder_1_out12),
    .out13(decoder_1_out13), .out14(decoder_1_out14), .out15(decoder_1_out15), .sel(WriteRegister),
    .en(RegWrite));  // open: out0
  Register #(.width(16)) register_1 (.D({16{1'b0}}), .en(1'b0), .Q(register_1_q), .clk(Clock), .clr(Reset));
  Register #(.width(16)) register_2 (.D(DataWrite), .en(decoder_1_out1), .Q(register_2_q), .clk(Clock), .clr(Reset));
  Register #(.width(16)) register_3 (.D(DataWrite), .en(decoder_1_out2), .Q(register_3_q), .clk(Clock), .clr(Reset));
  Register #(.width(16)) register_4 (.D(DataWrite), .en(decoder_1_out3), .Q(register_4_q), .clk(Clock), .clr(Reset));
  Register #(.width(16)) register_5 (.D(DataWrite), .en(decoder_1_out4), .Q(register_5_q), .clk(Clock), .clr(Reset));
  Register #(.width(16)) register_6 (.D(DataWrite), .en(decoder_1_out5), .Q(register_6_q), .clk(Clock), .clr(Reset));
  Register #(.width(16)) register_7 (.D(DataWrite), .en(decoder_1_out6), .Q(register_7_q), .clk(Clock), .clr(Reset));
  Register #(.width(16)) register_8 (.D(DataWrite), .en(decoder_1_out7), .Q(register_8_q), .clk(Clock), .clr(Reset));
  Register #(.width(16)) register_9 (.D(DataWrite), .en(decoder_1_out8), .Q(register_9_q), .clk(Clock), .clr(Reset));
  Register #(.width(16)) register_10 (.D(DataWrite), .en(decoder_1_out9), .Q(register_10_q), .clk(Clock), .clr(Reset));
  Register #(.width(16)) register_11 (.D(DataWrite), .en(decoder_1_out10), .Q(register_11_q), .clk(Clock), .clr(Reset));
  Register #(.width(16)) register_12 (.D(DataWrite), .en(decoder_1_out11), .Q(register_12_q), .clk(Clock), .clr(Reset));
  Register #(.width(16)) register_13 (.D(DataWrite), .en(decoder_1_out12), .Q(register_13_q), .clk(Clock), .clr(Reset));
  Register #(.width(16)) register_14 (.D(DataWrite), .en(decoder_1_out13), .Q(register_14_q), .clk(Clock), .clr(Reset));
  Register #(.width(16)) register_15 (.D(DataWrite), .en(decoder_1_out14), .Q(register_15_q), .clk(Clock), .clr(Reset));
  Register #(.width(16)) register_16 (.D(DataWrite), .en(decoder_1_out15), .Q(register_16_q), .clk(Clock), .clr(Reset));
  Multiplexer #(.select(4), .width(16)) multiplexer_1 (
    .in0(register_1_q), .in1(register_2_q), .in2(register_3_q), .in3(register_4_q), .in4(register_5_q),
    .in5(register_6_q), .in6(register_7_q), .in7(register_8_q), .in8(register_9_q), .in9(register_10_q),
    .in10(register_11_q), .in11(register_12_q), .in12(register_13_q), .in13(register_14_q),
    .in14(register_15_q), .in15(register_16_q), .out(DataRead1), .sel(ReadRegister1));  // open: en
  Multiplexer #(.select(4), .width(16)) multiplexer_2 (
    .in0(register_1_q), .in1(register_2_q), .in2(register_3_q), .in3(register_4_q), .in4(register_5_q),
    .in5(register_6_q), .in6(register_7_q), .in7(register_8_q), .in8(register_9_q), .in9(register_10_q),
    .in10(register_11_q), .in11(register_12_q), .in12(register_13_q), .in13(register_14_q),
    .in14(register_15_q), .in15(register_16_q), .out(DataRead2), .sel(ReadRegister2));  // open: en
endmodule

module shift (
  input  [3:0] in_1,
  output out_2
);

  wire SLL_out, SLR_out;

  and SLL (SLL_out, in_1[3], ~in_1[2], in_1[1], in_1[0]);  // AND_Gate
  and SLR (SLR_out, in_1[3], in_1[2], ~in_1[1], ~in_1[0]);  // AND_Gate
  or or_1 (out_2, SLL_out, SLR_out);
endmodule

module unitControl (
  input  [3:0] in_1,
  output RegDst,
  output ALUSrc,
  output MemtoReg,
  output RegWrite,
  output MemRead,
  output MenWrite,
  output Branch,
  output [1:0] ALUOp,
  output Jump
);

  wire and_2_out, and_3_out;

  and and_1 (RegDst, ~in_1[3], ~in_1[1], ~in_1[0]);  // AND_Gate
  and and_2 (and_2_out, in_1[3], ~in_1[2], ~in_1[1], ~in_1[0]);  // AND_Gate
  and and_3 (and_3_out, ~in_1[3], in_1[2], ~in_1[1], ~in_1[0]);  // AND_Gate
  and and_4 (MemtoReg, in_1[3], ~in_1[1], ~in_1[0]);  // AND_Gate
  and and_5 (RegWrite, ~in_1[2], ~in_1[1], ~in_1[0]);  // AND_Gate
  and and_6 (MemRead, in_1[3], ~in_1[2], ~in_1[1], ~in_1[0]);  // AND_Gate
  and and_7 (MenWrite, ~in_1[3], in_1[2], ~in_1[1], ~in_1[0]);  // AND_Gate
  and and_8 (Branch, in_1[3], in_1[2], ~in_1[1], ~in_1[0]);  // AND_Gate
  and and_9 (ALUOp[0], ~in_1[3], ~in_1[2], ~in_1[0]);  // AND_Gate
  and and_10 (ALUOp[1], in_1[3], in_1[2], ~in_1[1], ~in_1[0]);  // AND_Gate
  and and_11 (Jump, ~in_1[3], ~in_1[2], in_1[1], ~in_1[0]);  // AND_Gate
  or or_1 (ALUSrc, and_2_out, and_3_out);
endmodule

module ALU_CONTROL (
  input  [3:0] in_1,
  input  [1:0] in_2,
  output [2:0] out_3
);
endmodule

module unidadTemporal (
  input  [3:0] OpCode,
  output RegDst,
  output ALUSrc,
  output MemtoReg,
  output RegWrite,
  output MemRead,
  output MemWrite,
  output Branch,
  output ALUOp1,
  output ALUOp0,
  output Jump
);

  wire and_3_out, and_4_out, not_2_out, not_3_out, not_4_out, not_5_out, not_6_out, not_7_out, not_8_out,
       not_9_out;

  not not_1 (RegDst, OpCode[0]);
  not not_2 (not_2_out, OpCode[1]);
  not not_3 (not_3_out, OpCode[0]);
  not not_4 (not_4_out, OpCode[2]);
  not not_5 (not_5_out, OpCode[1]);
  not not_6 (not_6_out, OpCode[1]);
  not not_7 (not_7_out, OpCode[0]);
  and and_1 (Branch, OpCode[1], OpCode[0]);
  not not_8 (not_8_out, OpCode[1]);
  not not_9 (not_9_out, OpCode[0]);
  and and_2 (ALUOp0, OpCode[1], OpCode[0]);
  and and_3 (and_3_out, not_2_out, OpCode[0]);
  or or_1 (ALUSrc, and_3_out, and_4_out);
  and and_4 (and_4_out, OpCode[1], not_3_out);
  and and_5 (RegWrite, not_4_out, not_5_out);
  and and_6 (MemRead, not_6_out, OpCode[0]);
  and and_7 (MemWrite, OpCode[1], not_7_out);
  and and_8 (ALUOp1, not_8_out, not_9_out);

  assign Jump = OpCode[2];
  assign MemtoReg = OpCode[0];
endmodule
