// Logisim project controlALU.circ as structural Verilog
module Unit_Control (
  input  [3:0] DCBA,
  output RegDst,
  output ALUSrc,
  output MemtoReg,
  output RegWrite,
  output MemRead,
  output MenWrite,
  output Branch,
  output ALUOp1,
  output ALUOp2,
  output Jump
);

  wire and_2_out, and_3_out;

  and and_1 (RegDst, ~DCBA[3], ~DCBA[1], ~DCBA[0]);  // AND_Gate
  and and_2 (and_2_out, DCBA[3], ~DCBA[2], ~DCBA[1], ~DCBA[0]);  // AND_Gate
  and and_3 (and_3_out, ~DCBA[3], DCBA[2], ~DCBA[1], ~DCBA[0]);  // AND_Gate
  and and_4 (MemtoReg, DCBA[3], ~DCBA[1], ~DCBA[0]);  // AND_Gate
  and and_5 (RegWrite, ~DCBA[2], ~DCBA[1], ~DCBA[0]);  // AND_Gate
  and and_6 (MemRead, DCBA[3], ~DCBA[2], ~DCBA[1], ~DCBA[0]);  // AND_Gate
  and and_7 (MenWrite, ~DCBA[3], DCBA[2], ~DCBA[1], ~DCBA[0]);  // AND_Gate
  and and_8 (Branch, DCBA[3], DCBA[2], ~DCBA[1], ~DCBA[0]);  // AND_Gate
  and and_9 (ALUOp1, ~DCBA[3], ~DCBA[2], ~DCBA[0]);  // AND_Gate
  and and_10 (ALUOp2, DCBA[3], DCBA[2], ~DCBA[1], ~DCBA[0]);  // AND_Gate
  and and_11 (Jump, ~DCBA[3], ~DCBA[2], DCBA[1], ~DCBA[0]);  // AND_Gate
  or or_1 (ALUSrc, and_2_out, and_3_out);
endmodule

module ALU_Control (
  input  [5:0] in_1,
  output Y1,
  output Y2,
  output Y3
);

  wire and_1_out, and_2_out, and_3_out, and_4_out, and_5_out, and_6_out, and_7_out, and_8_out, and_9_out;

  and and_1 (and_1_out, ~in_1[0], in_1[1], in_1[2], ~in_1[3], ~in_1[5]);  // AND_Gate
  and and_2 (and_2_out, ~in_1[0], in_1[1], in_1[2], in_1[4], ~in_1[5]);  // AND_Gate
  and and_3 (and_3_out, ~in_1[0], in_1[1], ~in_1[2], in_1[3], ~in_1[4], ~in_1[5]);  // AND_Gate
  and and_4 (and_4_out, ~in_1[0], ~in_1[1]);  // AND_Gate
  and and_5 (and_5_out, ~in_1[0], in_1[2], ~in_1[4], ~in_1[5]);  // AND_Gate
  and and_6 (and_6_out, ~in_1[0], in_1[2], ~in_1[3], ~in_1[5]);  // AND_Gate
  and and_7 (and_7_out, ~in_1[0], ~in_1[2], in_1[3], in_1[4], ~in_1[5]);  // AND_Gate
  and and_8 (and_8_out, ~in_1[0], in_1[2], in_1[3], ~in_1[5]);  // AND_Gate
  and and_9 (and_9_out, ~in_1[0], ~in_1[3], in_1[4], ~in_1[5]);  // AND_Gate
  or or_1 (Y1, and_1_out, and_2_out, and_3_out);
  or or_2 (Y2, and_4_out, and_5_out, and_6_out, and_7_out);
  or or_3 (Y3, ~in_1[1], and_8_out, and_9_out);  // OR_Gate
endmodule
