// Logisim project laboratorio 1 final.circ as structural Verilog: 25 circuits, main circuit laboratorio 1
module laboratorio_1 (
  input  [2:0] S,
  input  [15:0] A,
  input  [15:0] B
);

  wire alu_16bits_1_overflow, alu_16bits_1_zero, d1_A, d1_B, d1_C, d1_D, d1_E, d1_F, d1_G, d2_A, d2_B, d2_C,
       d2_D, d2_E, d2_F, d2_G, d3_A, d3_B, d3_C, d3_D, d3_E, d3_F, d3_G, d4_A, d4_B, d4_C, d4_D, d4_E, d4_F,
       d4_G, d5_A, d5_B, d5_C, d5_D, d5_E, d5_F, d5_G, signo;
  wire [15:0] Resultado;

  LED led_1 (.in(alu_16bits_1_zero));
  ALU_16bits alu_16bits_1 (
    .ZERO(alu_16bits_1_zero), .overflow(alu_16bits_1_overflow), .A(A), .B(B), .Selector(S), .Result(Resultado));
  LED led_2 (.in(alu_16bits_1_overflow));
  _16bits_to_7seg _16bits_to_7seg (
    .in_1(Resultado), .signo(signo), .D1({d1_G, d1_F, d1_E, d1_D, d1_C, d1_B, d1_A}),
    .D1_2({d2_G, d2_F, d2_E, d2_D, d2_C, d2_B, d2_A}), .D1_3({d3_G, d3_F, d3_E, d3_D, d3_C, d3_B, d3_A}),
    .D1_4({d4_G, d4_F, d4_E, d4_D, d4_C, d4_B, d4_A}), .D1_5({d5_G, d5_F, d5_E, d5_D, d5_C, d5_B, d5_A}));
  LED led_3 (.in(Resultado[14]));
  LED led_4 (.in(Resultado[13]));
  LED led_5 (.in(Resultado[15]));
  LED Negativo (.in(signo));
  LED led_6 (.in(Resultado[11]));
  LED led_7 (.in(Resultado[12]));
  LED led_8 (.in(Resultado[10]));
  _7_Segment_Display u_7_segment_display_1 (
    .g(d5_G), .f(d5_F), .a(d5_A), .b(d5_B), .e(d5_E), .d(d5_D), .c(d5_C));  // open: dp
  LED led_9 (.in(Resultado[8]));
  LED led_10 (.in(Resultado[9]));
  _7_Segment_Display u_7_segment_display_2 (
    .g(d4_G), .f(d4_F), .a(d4_A), .b(d4_B), .e(d4_E), .d(d4_D), .c(d4_C));  // open: dp
  LED led_11 (.in(Resultado[6]));
  LED led_12 (.in(Resultado[5]));
  LED led_13 (.in(Resultado[7]));
  _7_Segment_Display u_7_segment_display_3 (
    .g(d3_G), .f(d3_F), .a(d3_A), .b(d3_B), .e(d3_E), .d(d3_D), .c(d3_C));  // open: dp
  LED led_14 (.in(Resultado[4]));
  LED led_15 (.in(Resultado[2]));
  LED led_16 (.in(Resultado[3]));
  _7_Segment_Display u_7_segment_display_4 (
    .g(d2_G), .f(d2_F), .a(d2_A), .b(d2_B), .e(d2_E), .d(d2_D), .c(d2_C));  // open: dp
  LED led_17 (.in(Resultado[0]));
  LED led_18 (.in(Resultado[1]));
  _7_Segment_Display u_7_segment_display_5 (
    .g(d1_G), .f(d1_F), .a(d1_A), .b(d1_B), .e(d1_E), .d(d1_D), .c(d1_C));  // open: dp
endmodule

module sumador_1bit (
  input  A,
  input  B,
  input  Cin,
  output S,
  output Cout
);

  wire and_1_out, and_2_out, and_3_out, and_4_out, and_5_out, and_6_out, and_7_out, not_1_out, not_2_out,
       not_3_out;

  not not_1 (not_1_out, A);
  not not_2 (not_2_out, B);
  not not_3 (not_3_out, Cin);
  and and_1 (and_1_out, not_1_out, not_2_out, Cin);
  and and_2 (and_2_out, not_1_out, B, not_3_out);
  and and_3 (and_3_out, A, not_2_out, not_3_out);
  and and_4 (and_4_out, A, B, Cin);
  and and_5 (and_5_out, B, Cin);
  and and_6 (and_6_out, A, B);
  and and_7 (and_7_out, A, Cin);
  or or_1 (S, and_1_out, and_2_out, and_3_out, and_4_out);
  or or_2 (Cout, and_5_out, and_6_out, and_7_out);
endmodule

module sumador_1bit_overflow (
  input  A,
  input  B,
  input  Cin,
  output S,
  output Cout,
  output overflow
);

  wire and_1_out, and_2_out, and_3_out, and_4_out, and_5_out, and_6_out, and_7_out, and_8_out, and_9_out,
       not_1_out, not_2_out, not_3_out, not_4_out;

  not not_1 (not_1_out, A);
  not not_2 (not_2_out, B);
  not not_3 (not_3_out, Cin);
  not not_4 (not_4_out, Cout);
  and and_1 (and_1_out, not_1_out, not_2_out, Cin);
  and and_2 (and_2_out, not_1_out, B, not_3_out);
  and and_3 (and_3_out, A, not_2_out, not_3_out);
  and and_4 (and_4_out, A, B, Cin);
  and and_5 (and_5_out, B, Cin);
  and and_6 (and_6_out, A, B);
  and and_7 (and_7_out, A, Cin);
  and and_8 (and_8_out, not_3_out, Cout);
  and and_9 (and_9_out, Cin, not_4_out);
  or or_1 (S, and_1_out, and_2_out, and_3_out, and_4_out);
  or or_2 (Cout, and_5_out, and_6_out, and_7_out);
  or or_3 (overflow, and_8_out, and_9_out);
endmodule

module sumador_2bits (
  input  [1:0] A,
  input  [1:0] B,
  input  Cin,
  output [1:0] S,
  output Cout
);

  wire Cout_t;

  sumador_1bit sumador_1bit (.A(A[0]), .B(B[0]), .Cin(Cin), .S(S[0]), .Cout(Cout_t));
  sumador_1bit sumador_1bit_2 (.A(A[1]), .B(B[1]), .Cin(Cout_t), .S(S[1]), .Cout(Cout));
endmodule

module sumador_2bits_overflow (
  input  [1:0] A,
  input  [1:0] B,
  input  Cin,
  output [1:0] S,
  output Cout,
  output Overflow
);

  wire Cout_t;

  sumador_1bit sumador_1bit (.A(A[0]), .B(B[0]), .Cin(Cin), .S(S[0]), .Cout(Cout_t));
  sumador_1bit_overflow sumador_1bit_overflow (
    .A(A[1]), .B(B[1]), .Cin(Cout_t), .S(S[1]), .Cout(Cout), .overflow(Overflow));
endmodule

module sumador_de_4bits (
  input  [3:0] A,
  input  [3:0] B,
  input  Cin,
  output [3:0] S,
  output Cout
);

  wire Cout_t;

  sumador_2bits sumador_de_2bits (.S(S[1:0]), .Cout(Cout_t), .A(A[1:0]), .B(B[1:0]), .Cin(Cin));
  sumador_2bits sumador_de_2bits_2 (.S(S[3:2]), .Cout(Cout), .A(A[3:2]), .B(B[3:2]), .Cin(Cout_t));
endmodule

module sumador_4bits_overflow (
  input  [3:0] A,
  input  [3:0] B,
  input  Cin,
  output [3:0] S,
  output Cout,
  output overflow
);

  wire Cout_t;

  sumador_2bits sumador_de_2bits (.S(S[1:0]), .Cout(Cout_t), .A(A[1:0]), .B(B[1:0]), .Cin(Cin));
  sumador_2bits_overflow sumador_de_2bits_overflow (
    .S(S[3:2]), .Cout(Cout), .Overflow(overflow), .A(A[3:2]), .B(B[3:2]), .Cin(Cout_t));
  // Probe on S
endmodule

module sumador_16bit_overflow (
  input  Cin,
  input  [15:0] A,
  input  [15:0] B,
  output [15:0] S,
  output Cout,
  output overflow
);

  wire Cout1, Cout2, Cout3;

  sumador_de_4bits sumador_de_4bits (.S(S[3:0]), .Cout(Cout1), .A(A[3:0]), .B(B[3:0]), .Cin(Cin));
  sumador_de_4bits sumador_de_4bits_2 (.S(S[7:4]), .Cout(Cout2), .A(A[7:4]), .B(B[7:4]), .Cin(Cout1));
  sumador_de_4bits sumador_de_4bits_3 (.S(S[11:8]), .Cout(Cout3), .A(A[11:8]), .B(B[11:8]), .Cin(Cout2));
  sumador_4bits_overflow sumador_de_4bits_overflow (
    .S(S[15:12]), .Cout(Cout), .overflow(overflow), .A(A[15:12]), .B(B[15:12]), .Cin(Cout3));
endmodule

module SLR_16bits (
  input  [15:0] A,
  input  [15:0] B,
  output [15:0] out_3
);

  wire S;
  wire [3:0] X, Y;
  wire [15:0] Decodificador_4bits_out_2, divider_1_out;

  OR_4bits or_4bits_1 (.Result(X), .A(B[7:4]), .B(B[11:8]));
  OR_4bits or_4bits_2 (.Result(Y), .A(B[15:12]), .B(X));
  or or_1 (S, Y[0], Y[1], Y[2], Y[3]);
  Decodificador_4bits Decodificador_4bits (.out_2(Decodificador_4bits_out_2), .in_1(B[3:0]));
  Divider #(.width(16)) divider_1 (.a(A), .b(Decodificador_4bits_out_2), .out(divider_1_out));  // open: upper, rem
  Multiplexer #(.width(16)) multiplexer_1 (.in0(divider_1_out), .in1({16{1'b0}}), .out(out_3), .sel(S));  // open: en

  // Other names for the same wires on the sheet: _1 = B[0]; B0[3:0] = B[3:0]; _2 = B[1]; _4 = B[2]; _8 = B[3];
  //   Result[15:0] = out_3
endmodule

module SLL_16bits (
  input  [15:0] A,
  input  [15:0] B,
  output [15:0] out_3
);

  SLR_16bits SLR_16bits (
    .out_3({out_3[0], out_3[1], out_3[2], out_3[3], out_3[4], out_3[5], out_3[6], out_3[7], out_3[8], out_3[9], out_3[10], out_3[11], out_3[12], out_3[13], out_3[14], out_3[15]}),
    .A({A[0], A[1], A[2], A[3], A[4], A[5], A[6], A[7], A[8], A[9], A[10], A[11], A[12], A[13], A[14], A[15]}),
    .B(B));
endmodule

module ALU_1bit_F (
  input  A,
  input  B,
  input  Cin,
  input  [2:0] in_4,
  input  SLT,
  output Result,
  output Cout,
  output overflow,
  output SLT_2
);

  wire AND, multiplexer_1_out, NOR, not_1_out, OR, RESTA;

  not not_1 (not_1_out, B);
  Multiplexer #(.select(3), .enable("false")) multiplexer_1 (
    .in0(B), .in1(B), .in2(B), .in3(B), .in4(not_1_out), .in5(B), .in6(not_1_out), .in7(B),
    .out(multiplexer_1_out), .sel(in_4));
  and and_1 (AND, A, B);
  or or_1 (OR, A, B);
  sumador_1bit_overflow sumador_1bit (
    .A(A), .B(multiplexer_1_out), .Cin(Cin), .S(RESTA), .Cout(Cout), .overflow(overflow));
  not not_2 (NOR, OR);
  XOR_1bit xor_1bit_1 (.A(overflow), .B(RESTA), .S(SLT_2));
  Multiplexer #(.select(3), .enable("false")) multiplexer_2 (
    .in0(NOR), .in1(OR), .in2(1'b0), .in3(AND), .in4(SLT), .in5(RESTA), .in6(RESTA), .in7(1'b0),
    .out(Result), .sel(in_4));

  // Other names for the same wires on the sheet: Selector[2:0] = in_4; SUMA = RESTA
endmodule

module ALU_16bits (
  input  [2:0] Selector,
  input  [15:0] A,
  input  [15:0] B,
  output [15:0] Result,
  output ZERO,
  output overflow
);

  wire alu_1bit_f_1_cout, alu_1bit_f_2_cout, alu_1bit_f_3_cout, alu_1bit_f_4_cout, alu_1bit_f_5_cout,
       alu_1bit_f_6_cout, alu_1bit_f_7_cout, alu_1bit_f_8_cout, alu_1bit_f_9_cout, alu_1bit_f_10_cout,
       alu_1bit_f_11_cout, alu_1bit_f_12_cout, alu_1bit_f_13_cout, alu_1bit_f_14_cout, alu_1bit_f_15_cout,
       alu_1bit_f_16_cout, Cin, not_1_out, or_1_out, SLT;
  wire [15:0] alu_1bit_f_1_result, SLL, SLR;

  ALU_1bit_F alu_1bit_f_1 (
    .Result(alu_1bit_f_1_result[0]), .Cout(alu_1bit_f_1_cout), .A(A[0]), .B(B[0]), .Cin(Cin),
    .in_4(Selector), .SLT(SLT));  // open: overflow, SLT_2
  ALU_1bit_F alu_1bit_f_2 (
    .Result(alu_1bit_f_1_result[1]), .Cout(alu_1bit_f_2_cout), .A(A[1]), .B(B[1]), .Cin(alu_1bit_f_1_cout),
    .in_4(Selector), .SLT(1'b0));  // open: overflow, SLT_2
  ALU_1bit_F alu_1bit_f_3 (
    .Result(alu_1bit_f_1_result[2]), .Cout(alu_1bit_f_3_cout), .A(A[2]), .B(B[2]), .Cin(alu_1bit_f_2_cout),
    .in_4(Selector), .SLT(1'b0));  // open: overflow, SLT_2
  ALU_1bit_F alu_1bit_f_4 (
    .Result(alu_1bit_f_1_result[3]), .Cout(alu_1bit_f_4_cout), .A(A[3]), .B(B[3]), .Cin(alu_1bit_f_3_cout),
    .in_4(Selector), .SLT(1'b0));  // open: overflow, SLT_2
  ALU_1bit_F alu_1bit_f_5 (
    .Result(alu_1bit_f_1_result[4]), .Cout(alu_1bit_f_5_cout), .A(A[4]), .B(B[4]), .Cin(alu_1bit_f_4_cout),
    .in_4(Selector), .SLT(1'b0));  // open: overflow, SLT_2
  ALU_1bit_F alu_1bit_f_6 (
    .Result(alu_1bit_f_1_result[5]), .Cout(alu_1bit_f_6_cout), .A(A[5]), .B(B[5]), .Cin(alu_1bit_f_5_cout),
    .in_4(Selector), .SLT(1'b0));  // open: overflow, SLT_2
  ALU_1bit_F alu_1bit_f_7 (
    .Result(alu_1bit_f_1_result[6]), .Cout(alu_1bit_f_7_cout), .A(A[6]), .B(B[6]), .Cin(alu_1bit_f_6_cout),
    .in_4(Selector), .SLT(1'b0));  // open: overflow, SLT_2
  ALU_1bit_F alu_1bit_f_8 (
    .Result(alu_1bit_f_1_result[7]), .Cout(alu_1bit_f_8_cout), .A(A[7]), .B(B[7]), .Cin(alu_1bit_f_7_cout),
    .in_4(Selector), .SLT(1'b0));  // open: overflow, SLT_2
  ALU_1bit_F alu_1bit_f_9 (
    .Result(alu_1bit_f_1_result[8]), .Cout(alu_1bit_f_9_cout), .A(A[8]), .B(B[8]), .Cin(alu_1bit_f_8_cout),
    .in_4(Selector), .SLT(1'b0));  // open: overflow, SLT_2
  ALU_1bit_F alu_1bit_f_10 (
    .Result(alu_1bit_f_1_result[9]), .Cout(alu_1bit_f_10_cout), .A(A[9]), .B(B[9]), .Cin(alu_1bit_f_9_cout),
    .in_4(Selector), .SLT(1'b0));  // open: overflow, SLT_2
  ALU_1bit_F alu_1bit_f_11 (
    .Result(alu_1bit_f_1_result[10]), .Cout(alu_1bit_f_11_cout), .A(A[10]), .B(B[10]),
    .Cin(alu_1bit_f_10_cout), .in_4(Selector), .SLT(1'b0));  // open: overflow, SLT_2
  ALU_1bit_F alu_1bit_f_12 (
    .Result(alu_1bit_f_1_result[11]), .Cout(alu_1bit_f_12_cout), .A(A[11]), .B(B[11]),
    .Cin(alu_1bit_f_11_cout), .in_4(Selector), .SLT(1'b0));  // open: overflow, SLT_2
  ALU_1bit_F alu_1bit_f_13 (
    .Result(alu_1bit_f_1_result[12]), .Cout(alu_1bit_f_13_cout), .A(A[12]), .B(B[12]),
    .Cin(alu_1bit_f_12_cout), .in_4(Selector), .SLT(1'b0));  // open: overflow, SLT_2
  ALU_1bit_F alu_1bit_f_14 (
    .Result(alu_1bit_f_1_result[13]), .Cout(alu_1bit_f_14_cout), .A(A[13]), .B(B[13]),
    .Cin(alu_1bit_f_13_cout), .in_4(Selector), .SLT(1'b0));  // open: overflow, SLT_2
  ALU_1bit_F alu_1bit_f_15 (
    .Result(alu_1bit_f_1_result[14]), .Cout(alu_1bit_f_15_cout), .A(A[14]), .B(B[14]),
    .Cin(alu_1bit_f_14_cout), .in_4(Selector), .SLT(1'b0));  // open: overflow, SLT_2
  ALU_1bit_F alu_1bit_f_16 (
    .Result(alu_1bit_f_1_result[15]), .Cout(alu_1bit_f_16_cout), .overflow(overflow), .A(A[15]), .B(B[15]),
    .Cin(alu_1bit_f_15_cout), .in_4(Selector), .SLT(1'b0), .SLT_2(SLT));
  SLL_16bits sll_16bits_1 (.B(B), .out_3(SLL), .A(A));
  SLR_16bits slr_16bits_1 (.out_3(SLR), .A(A), .B(B));
  Multiplexer #(.select(3), .width(16)) multiplexer_1 (
    .in0(alu_1bit_f_1_result), .in1(alu_1bit_f_1_result), .in2(SLL), .in3(alu_1bit_f_1_result),
    .in4(alu_1bit_f_1_result), .in5(alu_1bit_f_1_result), .in6(alu_1bit_f_1_result), .in7(SLR), .out(Result),
    .sel(Selector));  // open: en
  not not_1 (not_1_out, 1'b0);
  Multiplexer #(.select(3), .enable("false")) multiplexer_2 (
    .in0(1'b0), .in1(1'b0), .in2(1'b0), .in3(1'b0), .in4(not_1_out), .in5(1'b0), .in6(not_1_out), .in7(1'b0),
    .out(Cin), .sel(Selector));
  or or_1 (or_1_out, Result[0], Result[1], Result[2], Result[3], Result[4], Result[5], Result[6], Result[7], Result[8], Result[9], Result[10], Result[11], Result[12], Result[13], Result[14], Result[15]);
  not not_2 (ZERO, or_1_out);
  // also tied to GND on the sheet: alu_1bit_f_16_cout
endmodule

module XOR_1bit (
  input  A,
  input  B,
  output S
);

  wire and_1_out, and_2_out, not_1_out, not_2_out;

  not not_1 (not_1_out, A);
  not not_2 (not_2_out, B);
  and and_1 (and_1_out, not_1_out, B);
  and and_2 (and_2_out, A, not_2_out);
  or or_1 (S, and_1_out, and_2_out);
endmodule

module OR_4bits (
  input  [3:0] A,
  input  [3:0] B,
  output [3:0] Result
);

  or or_1 (Result[0], A[0], B[0]);
  or or_2 (Result[1], A[1], B[1]);
  or or_3 (Result[2], A[2], B[2]);
  or or_4 (Result[3], A[3], B[3]);
endmodule

module Decodificador_4bits (
  input  [3:0] in_1,
  output [15:0] out_2
);

  // Probe on in_1
  and and_1 (out_2[0], ~in_1[0], ~in_1[1], ~in_1[2], ~in_1[3]);  // AND_Gate
  and and_2 (out_2[1], in_1[0], ~in_1[1], ~in_1[2], ~in_1[3]);  // AND_Gate
  and and_3 (out_2[2], ~in_1[0], in_1[1], ~in_1[2], ~in_1[3]);  // AND_Gate
  and and_4 (out_2[3], in_1[0], in_1[1], ~in_1[2], ~in_1[3]);  // AND_Gate
  and and_5 (out_2[4], ~in_1[0], ~in_1[1], in_1[2], ~in_1[3]);  // AND_Gate
  and and_6 (out_2[5], in_1[0], ~in_1[1], in_1[2], ~in_1[3]);  // AND_Gate
  and and_7 (out_2[6], ~in_1[0], in_1[1], in_1[2], ~in_1[3]);  // AND_Gate
  and and_8 (out_2[7], in_1[0], in_1[1], in_1[2], ~in_1[3]);  // AND_Gate
  and and_9 (out_2[8], ~in_1[0], ~in_1[1], ~in_1[2], in_1[3]);  // AND_Gate
  and and_10 (out_2[9], in_1[0], ~in_1[1], ~in_1[2], in_1[3]);  // AND_Gate
  and and_11 (out_2[10], ~in_1[0], in_1[1], ~in_1[2], in_1[3]);  // AND_Gate
  and and_12 (out_2[11], in_1[0], in_1[1], ~in_1[2], in_1[3]);  // AND_Gate
  and and_13 (out_2[12], ~in_1[0], ~in_1[1], in_1[2], in_1[3]);  // AND_Gate
  and and_14 (out_2[13], in_1[0], ~in_1[1], in_1[2], in_1[3]);  // AND_Gate
  and and_15 (out_2[14], ~in_1[0], in_1[1], in_1[2], in_1[3]);  // AND_Gate
  and and_16 (out_2[15], in_1[0], in_1[1], in_1[2], in_1[3]);
  // Probe on out_2
endmodule

module Convert_16bits_bcd (
  input  [15:0] \input ,
  output signo,
  output [15:0] S,
  output [3:0] digito
);

  wire [15:0] magnitud, not_1_out, sumador_16bits_s;
  wire [15:4] divider_1_rem;

  assign not_1_out = ~\input ;  // NOT_Gate not_1, 16 bits wide
  sumador_16bit_overflow sumador_16bits (
    .S(sumador_16bits_s), .A(not_1_out), .B(16'h1), .Cin(1'b0));  // open: Cout, overflow
  Multiplexer #(.width(16)) multiplexer_1 (
    .in0(\input ), .in1(sumador_16bits_s), .out(magnitud), .sel(\input [15]));  // open: en
  Divider #(.width(16)) divider_1 (.a(magnitud), .b(16'ha), .out(S), .rem({divider_1_rem, digito}));  // open: upper

  assign signo = \input [15];

  // Other names for the same wires on the sheet: Negativo = \input [15]
endmodule

// A
module segmento_A (
  input  [3:0] \input ,
  output A
);

  wire and_1_out, and_2_out, or_1_out;

  and and_1 (and_1_out, ~\input [3], ~\input [2], ~\input [1], \input [0]);  // AND_Gate
  and and_2 (and_2_out, ~\input [3], \input [2], ~\input [1], ~\input [0]);  // AND_Gate
  not not_1 (A, or_1_out);
  or or_1 (or_1_out, and_1_out, and_2_out);
endmodule

// B
module segmento_B (
  input  [3:0] \input ,
  output B
);

  wire and_1_out, and_2_out, or_1_out;

  and and_1 (and_1_out, ~\input [3], \input [2], ~\input [1], \input [0]);  // AND_Gate
  and and_2 (and_2_out, ~\input [3], \input [2], \input [1], ~\input [0]);  // AND_Gate
  or or_1 (or_1_out, and_1_out, and_2_out);
  not not_1 (B, or_1_out);
endmodule

// C
module segmento_C (
  input  [3:0] \input ,
  output C
);

  wire and_1_out;

  and and_1 (and_1_out, ~\input [3], ~\input [2], \input [1], ~\input [0]);  // AND_Gate
  not not_1 (C, and_1_out);
endmodule

// D
module segmento_D (
  input  [3:0] \input ,
  output D
);

  wire and_1_out, and_2_out, and_3_out, or_1_out;

  and and_1 (and_1_out, ~\input [3], ~\input [2], ~\input [1], \input [0]);  // AND_Gate
  and and_2 (and_2_out, ~\input [3], \input [2], ~\input [1], ~\input [0]);  // AND_Gate
  and and_3 (and_3_out, ~\input [3], \input [2], \input [1], \input [0]);  // AND_Gate
  or or_1 (or_1_out, and_1_out, and_2_out, and_3_out);
  not not_1 (D, or_1_out);
endmodule

// E
module segmento_E (
  input  [3:0] \input ,
  output E
);

  wire and_1_out, and_2_out, and_3_out, or_1_out;

  and and_1 (and_1_out, ~\input [3], \input [0]);  // AND_Gate
  and and_2 (and_2_out, ~\input [2], ~\input [1], \input [0]);  // AND_Gate
  and and_3 (and_3_out, ~\input [3], \input [2], ~\input [1]);  // AND_Gate
  or or_1 (or_1_out, and_1_out, and_2_out, and_3_out);
  not not_1 (E, or_1_out);
endmodule

// F
module segmento_F (
  input  [3:0] \input ,
  output F
);

  wire and_1_out, and_2_out, and_3_out, or_1_out;

  and and_1 (and_1_out, ~\input [3], ~\input [2], \input [0]);  // AND_Gate
  and and_2 (and_2_out, ~\input [3], ~\input [2], \input [1]);  // AND_Gate
  and and_3 (and_3_out, ~\input [3], \input [1], \input [0]);  // AND_Gate
  or or_1 (or_1_out, and_1_out, and_2_out, and_3_out);
  not not_1 (F, or_1_out);
endmodule

// G
module segmento_G (
  input  [3:0] \input ,
  output G
);

  wire and_1_out, and_2_out, or_1_out;

  and and_1 (and_1_out, ~\input [3], ~\input [2], ~\input [1]);  // AND_Gate
  and and_2 (and_2_out, ~\input [3], \input [2], \input [1], \input [0]);  // AND_Gate
  or or_1 (or_1_out, and_1_out, and_2_out);
  not not_1 (G, or_1_out);
endmodule

module bcd_a_7_segmentos (
  input  [3:0] \input ,
  output [6:0] BCD
);

  segmento_A segmento_a_1 (.\input (\input ), .A(BCD[0]));
  segmento_B segmento_b_1 (.\input (\input ), .B(BCD[1]));
  segmento_C segmento_c_1 (.\input (\input ), .C(BCD[2]));
  segmento_D segmento_d_1 (.\input (\input ), .D(BCD[3]));
  segmento_E segmento_e_1 (.\input (\input ), .E(BCD[4]));
  segmento_F segmento_f_1 (.\input (\input ), .F(BCD[5]));
  segmento_G segmento_g_1 (.\input (\input ), .G(BCD[6]));
endmodule

module _16bits_to_7seg (
  input  [15:0] in_1,
  output signo,
  output [6:0] D1,
  output [6:0] D1_2,
  output [6:0] D1_3,
  output [6:0] D1_4,
  output [6:0] D1_5
);

  wire [3:0] _16bits_a_bcd_2_digito, _16bits_a_bcd_3_digito, _16bits_a_bcd_4_digito, _16bits_a_bcd_5_digito,
       _16bits_a_bcd_digito;
  wire [15:0] S1, S2, S3, S4;

  Convert_16bits_bcd _16bits_a_bcd (.\input (in_1), .signo(signo), .digito(_16bits_a_bcd_digito), .S(S1));
  Convert_16bits_bcd _16bits_a_bcd_2 (.\input (S1), .digito(_16bits_a_bcd_2_digito), .S(S2));  // open: signo
  Convert_16bits_bcd _16bits_a_bcd_3 (.\input (S2), .digito(_16bits_a_bcd_3_digito), .S(S3));  // open: signo
  Convert_16bits_bcd _16bits_a_bcd_4 (.\input (S3), .digito(_16bits_a_bcd_4_digito), .S(S4));  // open: signo
  Convert_16bits_bcd _16bits_a_bcd_5 (.\input (S4), .digito(_16bits_a_bcd_5_digito));  // open: signo, S
  bcd_a_7_segmentos bcd_a_7_segmentos_1 (.\input (_16bits_a_bcd_digito), .BCD(D1));
  bcd_a_7_segmentos bcd_a_7_segmentos_2 (.\input (_16bits_a_bcd_2_digito), .BCD(D1_2));
  bcd_a_7_segmentos bcd_a_7_segmentos_3 (.\input (_16bits_a_bcd_3_digito), .BCD(D1_3));
  bcd_a_7_segmentos bcd_a_7_segmentos_4 (.\input (_16bits_a_bcd_4_digito), .BCD(D1_4));
  bcd_a_7_segmentos bcd_a_7_segmentos_5 (.\input (_16bits_a_bcd_5_digito), .BCD(D1_5));
endmodule
